// Logisim project cpu.circ as structural Verilog: 3 circuits, main circuit main
module main (
  input  [15:0] INSTRUCTION,
  input  CLOCK,
  output [15:0] FETCH_ADDRESS,
  output [15:0] L_s0_Value_555821f6,
  output [15:0] L_s1_Value_bb868b5b,
  output [15:0] L_s2_Value_1029e135,
  output [15:0] L_ra_Value_3ae5280b,
  output [15:0] L_sp_Value_256d6ed0,
  output [15:0] L_HI_Value_4d3aacc1,
  output [15:0] L_LO_Value_6d74149f
);

  wire L_HI_108849eb_p1, L_HI_108849eb_p3, L_LO_6db75bec_p1, L_LO_6db75bec_p4;
  wire [15:0] adder_4_1_pc_out;

  Register #(.width(16)) L_PC_1fb09d07 (.D(adder_4_1_pc_out), .clk(CLOCK), .Q(FETCH_ADDRESS));  // open: en, clr
  Adder_4 adder_4_1 (.PC_in(FETCH_ADDRESS), .PC_out(adder_4_1_pc_out));
  Instruction_decoder instruction_decoder_1 (.Instruction(INSTRUCTION));  // open: rd, immediate, rs, rt, funct, opcode
  // regfile_main main_1: pin names not known
  // Register #(.width(16)) L_HI_108849eb: pin names not known; wires that end beside it: L_HI_108849eb_p1, L_s1_Value_bb868b5b, L_HI_108849eb_p3
  // alu_main main_2: pin names not known
  // mem_main MEM: pin names not known
  // Register #(.width(16)) L_LO_6db75bec: pin names not known; wires that end beside it: L_LO_6db75bec_p1, L_LO_6db75bec_p1, L_ra_Value_3ae5280b, L_LO_6db75bec_p4

  // Other names for the same wires on the sheet: clk = CLOCK; fetch_addr[15:0] = FETCH_ADDRESS

  // Notes on the sheet:
  //   Output
  //   These are outputs/inputs from run.circ
  //   Inputs
  //   These are DEBUG/TEST outputs from your circuit.
endmodule

module Adder_4 (
  input  [15:0] PC_in,
  output [15:0] PC_out
);

  Adder #(.width(16)) adder_1 (.a(PC_in), .b(16'h4), .out(PC_out));  // open: cin, cout
endmodule

module Instruction_decoder (
  input  [15:0] Instruction,
  output [2:0] funct,
  output [2:0] rt,
  output [2:0] rs,
  output [9:0] immediate,
  output [2:0] rd,
  output [3:0] opcode
);


  assign funct = Instruction[2:0];
  assign immediate = Instruction[9:0];
  assign opcode = Instruction[15:12];
  assign rd = Instruction[11:9];
  assign rs = Instruction[8:6];
  assign rt = Instruction[5:3];
endmodule
